# Fritzing sketch SoleBotPCBV1.1∂ (saved by Fritzing 0.9.3b)
circuit board: 18cm x 8.4cm
breadboards: 1

parts:
  Arduino_Nano = Arduino Nano (Rev3.0) (ICSP)
  Out_12_-_Cowbell = mosfet switch HW-548 modified pcb
  Out_11_-_Ride_Cymbal = mosfet switch HW-548 modified pcb
  Out_10_-Floor_Tom = mosfet switch HW-548 modified pcb
  Out_9_-_Rack_Tom = mosfet switch HW-548 modified pcb
  Out_8_-_Bottom_Hat_Up = mosfet switch HW-548 modified pcb
  Out_7_-_Top_Hat_Up = mosfet switch HW-548 modified pcb
  Out_6_-_Hat_Stick = mosfet switch HW-548 modified pcb
  Out_2_-_Stick_Click = mosfet switch HW-548 modified pcb
  Out_3_-_Kick_Beater = mosfet switch HW-548 modified pcb
  Out_4_-_Crash_Stick = mosfet switch HW-548 modified pcb
  Out_5_-_Snare_Stick = mosfet switch HW-548 modified pcb
  G_5V_24V = Header 3 [package=screwterminal-3.5mm-3_lock.007s]
  RX_TX_G = Header 3 [package=screwterminal-3.5mm-3_lock.007s]
  1k2Ω = Resistor [tolerance=±5% resistance=1.2k package=THT]
  LED1 = LED - 3mm [color="Red (633nm)" package="3 mm [THT]"]
  Reset = Pushbutton [package="[THT]"]
  ©2024_Crunchy = Resistor [tolerance=±5% resistance=220 package=THT]
  L1 = Inductor [package="400 mil [THT]"]
  A0_A7 = screw terminal, 8 pins

nets:
  N1: Arduino_Nano.D1/TX, RX_TX_G.2
  N2: Arduino_Nano.D0/RX, RX_TX_G.3
  N3: Arduino_Nano.D2, Out_2_-_Stick_Click.Pin_1, Out_2_-_Stick_Click.Pin_2, Out_2_-_Stick_Click.Pin_3
  N4: Arduino_Nano.D3, Out_3_-_Kick_Beater.Pin_1, Out_3_-_Kick_Beater.Pin_2, Out_3_-_Kick_Beater.Pin_3
  N5: Arduino_Nano.D4, Out_4_-_Crash_Stick.Pin_1, Out_4_-_Crash_Stick.Pin_2, Out_4_-_Crash_Stick.Pin_3
  N6: Arduino_Nano.D5, Out_5_-_Snare_Stick.Pin_1, Out_5_-_Snare_Stick.Pin_2, Out_5_-_Snare_Stick.Pin_3
  N7: Arduino_Nano.D6, Out_6_-_Hat_Stick.Pin_1, Out_6_-_Hat_Stick.Pin_2, Out_6_-_Hat_Stick.Pin_3
  N8: Arduino_Nano.D7, Out_7_-_Top_Hat_Up.Pin_1, Out_7_-_Top_Hat_Up.Pin_2, Out_7_-_Top_Hat_Up.Pin_3
  N9: Arduino_Nano.D8, Out_8_-_Bottom_Hat_Up.Pin_1, Out_8_-_Bottom_Hat_Up.Pin_2, Out_8_-_Bottom_Hat_Up.Pin_3
  N10: Arduino_Nano.D9, Out_9_-_Rack_Tom.Pin_1, Out_9_-_Rack_Tom.Pin_2, Out_9_-_Rack_Tom.Pin_3
  N11: Arduino_Nano.D10, Out_10_-Floor_Tom.Pin_1, Out_10_-Floor_Tom.Pin_2, Out_10_-Floor_Tom.Pin_3
  N12: Arduino_Nano.D11/MOSI, Out_11_-_Ride_Cymbal.Pin_1, Out_11_-_Ride_Cymbal.Pin_2, Out_11_-_Ride_Cymbal.Pin_3
  N13: Arduino_Nano.D12/MISO, Out_12_-_Cowbell.Pin_1, Out_12_-_Cowbell.Pin_2, Out_12_-_Cowbell.Pin_3
  N14: Arduino_Nano.GND, Out_12_-_Cowbell.Pin_4, Out_12_-_Cowbell.Pin_5, Out_12_-_Cowbell.Pin_6, Out_12_-_Cowbell.Pin_7, Out_12_-_Cowbell.Pin_9, Out_11_-_Ride_Cymbal.Pin_4, Out_11_-_Ride_Cymbal.Pin_5, Out_11_-_Ride_Cymbal.Pin_6, Out_11_-_Ride_Cymbal.Pin_7, Out_11_-_Ride_Cymbal.Pin_9, Out_10_-Floor_Tom.Pin_4, Out_10_-Floor_Tom.Pin_5, Out_10_-Floor_Tom.Pin_6, Out_10_-Floor_Tom.Pin_7, Out_10_-Floor_Tom.Pin_9, Out_9_-_Rack_Tom.Pin_4, Out_9_-_Rack_Tom.Pin_5, Out_9_-_Rack_Tom.Pin_6, Out_9_-_Rack_Tom.Pin_7, Out_9_-_Rack_Tom.Pin_9, Out_8_-_Bottom_Hat_Up.Pin_4, Out_8_-_Bottom_Hat_Up.Pin_5, Out_8_-_Bottom_Hat_Up.Pin_6, Out_8_-_Bottom_Hat_Up.Pin_7, Out_8_-_Bottom_Hat_Up.Pin_9, Out_7_-_Top_Hat_Up.Pin_4, Out_7_-_Top_Hat_Up.Pin_5, Out_7_-_Top_Hat_Up.Pin_6, Out_7_-_Top_Hat_Up.Pin_7, Out_7_-_Top_Hat_Up.Pin_9, Out_6_-_Hat_Stick.Pin_4, Out_6_-_Hat_Stick.Pin_5, Out_6_-_Hat_Stick.Pin_6, Out_6_-_Hat_Stick.Pin_7, Out_6_-_Hat_Stick.Pin_9, Out_2_-_Stick_Click.Pin_4, Out_2_-_Stick_Click.Pin_5, Out_2_-_Stick_Click.Pin_6, Out_2_-_Stick_Click.Pin_7, Out_2_-_Stick_Click.Pin_9, Out_3_-_Kick_Beater.Pin_4, Out_3_-_Kick_Beater.Pin_5, Out_3_-_Kick_Beater.Pin_6, Out_3_-_Kick_Beater.Pin_7, Out_3_-_Kick_Beater.Pin_9, Out_4_-_Crash_Stick.Pin_4, Out_4_-_Crash_Stick.Pin_5, Out_4_-_Crash_Stick.Pin_6, Out_4_-_Crash_Stick.Pin_7, Out_4_-_Crash_Stick.Pin_9, Out_5_-_Snare_Stick.Pin_4, Out_5_-_Snare_Stick.Pin_5, Out_5_-_Snare_Stick.Pin_6, Out_5_-_Snare_Stick.Pin_7, Out_5_-_Snare_Stick.Pin_9, G_5V_24V.1, RX_TX_G.1, 1k2Ω.Pin_1, Reset.Pin_3, Reset.Pin_4
  N15: Arduino_Nano.RESET, Reset.Pin_1, Reset.Pin_2
  N16: Arduino_Nano.5V, G_5V_24V.2
  N17: Arduino_Nano.A7, A0_A7.pin8
  N18: Arduino_Nano.A6, A0_A7.pin7
  N19: Arduino_Nano.A5, A0_A7.pin6
  N20: Arduino_Nano.A4, A0_A7.pin5
  N21: Arduino_Nano.A3, A0_A7.pin4
  N22: Arduino_Nano.A2, A0_A7.pin3
  N23: Arduino_Nano.A1, A0_A7.pin2
  N24: Arduino_Nano.A0, A0_A7.pin1
  N25: Arduino_Nano.D13/SCK, LED1.anode
  N26: Out_12_-_Cowbell.Pin_8, Out_11_-_Ride_Cymbal.Pin_8, Out_11_-_Ride_Cymbal.Pin_10, Out_10_-Floor_Tom.Pin_8, Out_10_-Floor_Tom.Pin_10, Out_9_-_Rack_Tom.Pin_8, Out_8_-_Bottom_Hat_Up.Pin_8, Out_7_-_Top_Hat_Up.Pin_8, Out_6_-_Hat_Stick.Pin_8, Out_2_-_Stick_Click.Pin_8, Out_2_-_Stick_Click.Pin_10, Out_3_-_Kick_Beater.Pin_8, Out_4_-_Crash_Stick.Pin_8, Out_5_-_Snare_Stick.Pin_8, G_5V_24V.3
  N27: 1k2Ω.Pin_0, LED1.cathode
  N28: ©2024_Crunchy.Pin_0, L1.pin_1
  N29: ©2024_Crunchy.Pin_1, L1.pin_0

notes:
  SoléBot V1.1∂
  MIDI Controlled Robotic Drumkit
  The "MarkMothersboard"
  + out -
  - out +

custom parts:
  mosfet switch HW-548 modified pcb: #548 Electronic switch control board pulse trigger switch DC controller module Field effect transistor power module. (Oct 2023 modified pcb to add pads for 4 of the terminal blocks.)
